# Fritzing sketch Primero_ESP8266 (saved by Fritzing 0.9.3b)
breadboards: 1

parts:
  Part1 = Arduino Uno (Rev3)
  U1 = ESP8266 WiFi Module [part_number=ESP8266]

nets:
  N1: Part1.D0/RX, U1.RXD
  N2: Part1.D1/TX, U1.TXD
  3V3: Part1.3V3, U1.VCC, U1.RST, U1.CH_PD
  GND: Part1.GND, U1.GND

custom parts:
  ESP8266 WiFi Module: Generic WiFi Module based on the ESP8266 with onboard PCB antenna and UART communications
